# Fritzing sketch tech hug vest diagrama (saved by Fritzing 1.0.4)
breadboards: 1

parts:
  Componente2 = Bluetooth HC-05 Macho
  LED1 = LED - 5mm [color="Red (633nm)" current=0.030A package="5 mm [THT]"]
  Componente3 = Arduino Mega 2560 (Rev3)
  R1 = Resistor [tolerance=±5% resistance=220 package="2010 [SMD]"]
  J1 = Basic Servo
  Componente4 = Breakout Board for Electret Microphone
  R2 = Basic Force Sensing Resistor (FSR) [package=THT]

nets:
  N1: Componente2.TXD, Componente3.D19/RX1
  N2: Componente2.RXD, Componente3.D18/TX1
  VCC: Componente2.VCC, Componente3.5V, J1.vcc, Componente4.VCC, R2.pin_2
  GND: Componente2.GND, LED1.cathode, Componente3.GND, J1.gnd, Componente4.GND, R2.pin_1
  N3: LED1.anode, R1.Pin_0
  N4: Componente3.A1, Componente4.AUD
  N5: Componente3.D4_PWM, J1.pulse
  N6: Componente3.D5_PWM, R1.Pin_1
